# Fritzing sketch Untitled Sketch (saved by Fritzing 0.9.3b)

parts:
  R3 = Resistor [tolerance=±5% resistance=220 package="2010 [SMD]"]
  Part1 = Arduino Uno (Rev3)
  Part2 = Triple Axis Accelerometer Breakout - ADXL345
  LED1 = smd LED [color="Red (633nm)" package="0603 [SMD]"]
  LED2 = smd LED [color="Red (633nm)" package="0603 [SMD]"]
  LED3 = smd LED [color="Red (633nm)" package="0603 [SMD]"]

nets:
  GND: R3.Pin_0, Part1.GND, Part2.GND
  N1: R3.Pin_1, LED1.cathode, LED2.cathode, LED3.cathode
  N2: Part1.A0, LED1.anode, LED2.anode, LED3.anode
  N3: Part1.A4/SDA, Part2.SDA
  N4: Part1.A5/SCL, Part2.SCL
  5V: Part1.5V, Part2.VCC
